# Fritzing sketch accelerophone3 (saved by Fritzing 0.9.3b)
circuit board: 12.683cm x 8.63257cm
breadboards: 2

parts:
  Arduino = Arduino Uno (Rev3)
  R1 = Resistor [tolerance=±5% resistance=220 package=THT]
  R2 = Resistor [tolerance=±5% resistance=220 package=THT]
  TCA9548A = Adafruit TCA9548A
  ACC01 = MMA8472_DealExtreme_CONNECTOR [package=1x08]
  ACC02 = MMA8472_DealExtreme_CONNECTOR [package=1x08]
  ACC05 = MMA8472_DealExtreme_CONNECTOR [package=1x08]
  ACC10 = MMA8472_DealExtreme_CONNECTOR [package=1x08]
  ACC13 = MMA8472_DealExtreme_CONNECTOR [package=1x08]
  ACC14 = MMA8472_DealExtreme_CONNECTOR [package=1x08]
  ACC06 = MMA8472_DealExtreme_CONNECTOR [package=1x08]
  ACC15 = MMA8472_DealExtreme_CONNECTOR [package=1x08]
  ACC16 = MMA8472_DealExtreme_CONNECTOR [package=1x08]
  ACC08 = MMA8472_DealExtreme_CONNECTOR [package=1x08]
  ACC07 = MMA8472_DealExtreme_CONNECTOR [package=1x08]
  ACC09 = MMA8472_DealExtreme_CONNECTOR [package=1x08]
  J1 = female pin header, 12 pins [form="♀ (female)"]
  J2 = female pin header, 12 pins [form="♀ (female)"]  # not connected
  ACC04 = MMA8472_DealExtreme_CONNECTOR [package=1x08]
  ACC12 = MMA8472_DealExtreme_CONNECTOR [package=1x08]
  ACC03 = MMA8472_DealExtreme_CONNECTOR [package=1x08]
  ACC11 = MMA8472_DealExtreme_CONNECTOR [package=1x08]

nets:
  N1: Arduino.A4/SDA, R1.Pin_1, TCA9548A.INPUTSDA
  N2: Arduino.A5/SCL, R2.Pin_1, TCA9548A.INPUTSCL
  3.3V: Arduino.3V3, R1.Pin_0, R2.Pin_0, TCA9548A.VCC, ACC01.3.3V, ACC01.SAO, ACC02.3.3V, ACC02.SAO, ACC05.3.3V, ACC05.SAO, ACC10.3.3V, ACC13.3.3V, ACC14.3.3V, ACC06.3.3V, ACC06.SAO, ACC15.3.3V, ACC16.3.3V, ACC08.3.3V, ACC08.SAO, ACC07.3.3V, ACC07.SAO, ACC09.3.3V, ACC04.3.3V, ACC04.SAO, ACC12.3.3V, ACC03.3.3V, ACC03.SAO, ACC11.3.3V
  GND: Arduino.GND, TCA9548A.GND, ACC01.GND, ACC02.GND, ACC05.GND, ACC10.GND, ACC10.SAO, ACC13.GND, ACC13.SAO, ACC14.GND, ACC14.SAO, ACC06.GND, ACC15.GND, ACC15.SAO, ACC16.GND, ACC16.SAO, ACC08.GND, ACC07.GND, ACC09.GND, ACC09.SAO, ACC04.GND, ACC12.GND, ACC12.SAO, ACC03.GND, ACC11.GND, ACC11.SAO
  N3: TCA9548A.2SDA, J1.pin1, ACC03.SDA, ACC11.SDA
  N4: TCA9548A.2SCL, J1.pin2, ACC03.SCL, ACC11.SCL
  N5: TCA9548A.3SDA, J1.pin3, ACC04.SDA, ACC12.SDA
  N6: TCA9548A.3SCL, J1.pin4, ACC04.SCL, ACC12.SCL
  N7: TCA9548A.4SDA, ACC05.SDA, ACC13.SDA, J1.pin5
  N8: TCA9548A.4SCL, ACC05.SCL, ACC13.SCL, J1.pin6
  N9: TCA9548A.5SDA, ACC14.SDA, ACC06.SDA, J1.pin7
  N10: TCA9548A.5SCL, ACC14.SCL, ACC06.SCL, J1.pin8
  N11: TCA9548A.6SDA, ACC15.SDA, ACC07.SDA, J1.pin9
  N12: TCA9548A.6SCL, ACC15.SCL, ACC07.SCL, J1.pin10
  N13: TCA9548A.7SDA, ACC16.SDA, ACC08.SDA, J1.pin11
  N14: TCA9548A.7SCL, ACC16.SCL, ACC08.SCL, J1.pin12
  N15: TCA9548A.0SDA, ACC01.SDA, ACC09.SDA
  N16: TCA9548A.0SCL, ACC01.SCL, ACC09.SCL
  N17: TCA9548A.1SDA, ACC02.SDA, ACC10.SDA
  N18: TCA9548A.1SCL, ACC02.SCL, ACC10.SCL

notes:
  SheepDog
  for QuadPack
  ACCELEROPHONE
  Feb-2018

custom parts:
  Adafruit TCA9548A: You just found the perfect I2C sensor, and you want to wire up two or three or more of them to your Arduino when you realize "Uh oh, this chip has a fixed I2C address, and from what I know about I2C, you cannot have two devices with the same address on the same SDA/SCL pins!" Are you out of luck? You would be, if you didn't have this ultra-cool TCA9548A 1-to-8 I2C multiplexer! Finally, a way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
  MMA8472_DealExtreme_CONNECTOR: Connector pel acceleròmetre triaxial MMA8452 comprat a Dealextreme (no és ni Sparkfun ni Adafruit)
