# Fritzing sketch accelerophone4 (saved by Fritzing 0.9.3b)
circuit board: 13.0904cm x 8.2719cm
breadboards: 1

parts:
  Acc4b = longpad pin header, 5 pins [form="long pad"]
  Acc4a = longpad pin header, 5 pins [form="long pad"]
  Acc3b = longpad pin header, 5 pins [form="long pad"]
  Acc3a = longpad pin header, 5 pins [form="long pad"]
  Acc7a = longpad pin header, 5 pins [form="long pad"]
  Acc7b = longpad pin header, 5 pins [form="long pad"]
  Acc8b = longpad pin header, 5 pins [form="long pad"]
  Acc8a = longpad pin header, 5 pins [form="long pad"]
  Acc6a = longpad pin header, 5 pins [form="long pad"]
  Acc6b = longpad pin header, 5 pins [form="long pad"]
  Acc5a = longpad pin header, 5 pins [form="long pad"]
  Acc5b = longpad pin header, 5 pins [form="long pad"]
  Acc1b = longpad pin header, 5 pins [form="long pad"]
  Acc1a = longpad pin header, 5 pins [form="long pad"]
  Acc2b = longpad pin header, 5 pins [form="long pad"]
  R2 = Resistor [tolerance=±5% resistance=330 package=THT]
  R1 = Resistor [tolerance=±5% resistance=330 package=THT]
  I2C_Expander = Adafruit TCA9548A
  Part1 = Arduino Uno (Rev3)
  Acc2a = longpad pin header, 5 pins [form="long pad"]
  J10 = longpad pin header, 12 pins [form="long pad"]
  J9 = longpad pin header, 12 pins [form="long pad"]

nets:
  VCC: Acc4b.pin1, Acc4a.pin1, Acc4a.pin5, Acc3b.pin1, Acc3a.pin1, Acc3a.pin5, Acc7a.pin1, Acc7a.pin5, Acc7b.pin1, Acc8b.pin1, Acc8a.pin1, Acc8a.pin5, Acc6a.pin1, Acc6a.pin5, Acc6b.pin1, Acc5a.pin1, Acc5a.pin5, Acc5b.pin1, Acc1b.pin1, Acc1a.pin1, Acc1a.pin5, Acc2b.pin1, R2.Pin_1, R1.Pin_1, I2C_Expander.VCC, Part1.3V3, Acc2a.pin1, Acc2a.pin5, J9.pin1
  GND: Acc4b.pin2, Acc4b.pin5, Acc4a.pin2, Acc3b.pin2, Acc3b.pin5, Acc3a.pin2, Acc7a.pin2, Acc7b.pin2, Acc7b.pin5, Acc8b.pin2, Acc8b.pin5, Acc8a.pin2, Acc6a.pin2, Acc6b.pin2, Acc6b.pin5, Acc5a.pin2, Acc5b.pin2, Acc5b.pin5, Acc1b.pin2, Acc1b.pin5, Acc1a.pin2, Acc2b.pin2, Acc2b.pin5, I2C_Expander.GND, Part1.GND, Acc2a.pin2, J9.pin2
  N1: Acc4b.pin3, Acc4a.pin3, I2C_Expander.3SCL, J10.pin9
  N2: Acc4b.pin4, Acc4a.pin4, I2C_Expander.3SDA, J10.pin10
  N3: Acc3b.pin3, Acc3a.pin3, I2C_Expander.2SCL, J10.pin11
  N4: Acc3b.pin4, Acc3a.pin4, I2C_Expander.2SDA, J10.pin12
  N5: Acc7a.pin3, Acc7b.pin3, I2C_Expander.6SCL, J10.pin3
  N6: Acc7a.pin4, Acc7b.pin4, I2C_Expander.6SDA, J10.pin4
  N7: Acc8b.pin3, Acc8a.pin3, I2C_Expander.7SCL, J10.pin1
  N8: Acc8b.pin4, Acc8a.pin4, I2C_Expander.7SDA, J10.pin2
  N9: Acc6a.pin3, Acc6b.pin3, I2C_Expander.5SCL, J10.pin5
  N10: Acc6a.pin4, Acc6b.pin4, I2C_Expander.5SDA, J10.pin6
  N11: Acc5a.pin3, Acc5b.pin3, I2C_Expander.4SCL, J10.pin7
  N12: Acc5a.pin4, Acc5b.pin4, I2C_Expander.4SDA, J10.pin8
  N13: Acc1b.pin3, Acc1a.pin3, I2C_Expander.0SCL, J9.pin10
  N14: Acc1b.pin4, Acc1a.pin4, I2C_Expander.0SDA, J9.pin9
  N15: Acc2b.pin3, I2C_Expander.1SCL, Acc2a.pin3, J9.pin12
  N16: Acc2b.pin4, I2C_Expander.1SDA, Acc2a.pin4, J9.pin11
  N17: R2.Pin_0, I2C_Expander.INPUTSCL, Part1.A5/SCL, J9.pin4
  N18: R1.Pin_0, I2C_Expander.INPUTSDA, Part1.A4/SDA, J9.pin3
  N19: I2C_Expander.RESET, J9.pin5
  N20: I2C_Expander.A0, J9.pin6
  N21: I2C_Expander.A1, J9.pin7
  N22: I2C_Expander.A2, J9.pin8

notes:
  3.3V
  Feb-2018
  ACCELEROPHONE
  SheepDog
  for QuadPack
  GND
  SDA
  SCL

custom parts:
  Adafruit TCA9548A: You just found the perfect I2C sensor, and you want to wire up two or three or more of them to your Arduino when you realize "Uh oh, this chip has a fixed I2C address, and from what I know about I2C, you cannot have two devices with the same address on the same SDA/SCL pins!" Are you out of luck? You would be, if you didn't have this ultra-cool TCA9548A 1-to-8 I2C multiplexer! Finally, a way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
